// Digital circuit 1_mux8a1.dig as structural Verilog
module _1_mux8a1 (
  input  S0,
  input  S1,
  input  S2,
  input  P0,
  input  P1,
  input  P2,
  input  P3,
  input  P4,
  input  P5,
  input  P6,
  input  P7,
  output Output
);

  wire and_1_out, and_2_out, and_3_out, and_4_out, and_5_out, and_6_out, and_7_out, and_8_out, or_1_out,
       or_2_out, S0_t, S1_t, S2_t;

  not not_1 (S2_t, S2);
  not not_2 (S1_t, S1);
  not not_3 (S0_t, S0);
  and and_1 (and_1_out, P0, S0_t, S1_t, S2_t);
  and and_2 (and_2_out, P1, S0, S1_t, S2_t);
  and and_3 (and_3_out, P2, S0_t, S1, S2_t);
  and and_4 (and_4_out, P3, S0, S1, S2_t);
  and and_5 (and_5_out, P4, S0_t, S1_t, S2);
  and and_6 (and_6_out, P5, S0, S1_t, S2);
  and and_7 (and_7_out, P6, S0_t, S1, S2);
  and and_8 (and_8_out, P7, S0, S1, S2);
  or or_1 (or_1_out, and_1_out, and_2_out, and_3_out, and_4_out);
  or or_2 (or_2_out, and_5_out, and_6_out, and_7_out, and_8_out);
  or or_3 (Output, or_1_out, or_2_out);

  // Notes on the sheet:
  //   Sección de entradas.
  //   Sección de seleción.
  //   Recibe el número (en binario)
  //   de la entrada que se quiere habilitar
  //   Circuito.
  //   Mediante compuertas AND y OR de máximo
  //   4 entradas, se encarga de recibir el número
  //   (en binario) de la salida a habilitar y permite 
  //   su flujo.
endmodule
