// Digital circuit 2_demux1a4.dig as structural Verilog
module _2_demux1a4 (
  input  Input,
  input  S1,
  input  S0,
  output P0,
  output P1,
  output P2,
  output P3
);

  wire S0_t, S1_t;

  not not_1 (S1_t, S1);
  not not_2 (S0_t, S0);
  and and_1 (P0, Input, S0_t, S1_t);
  and and_2 (P1, Input, S0, S1_t);
  and and_3 (P2, Input, S0_t, S1);
  and and_4 (P3, Input, S0, S1);

  // Other names for the same wires on the sheet: I = Input

  // Notes on the sheet:
  //   Sección de selección.
  //   Recibe el número (en binario) de
  //   la salida que se quiere habilitar.
  //   Circuito
  //   Habilita la salida correspondiente al número
  //   ingresado (en binario)
endmodule
