// Digital circuit 3a_rsFlipFlop.dig as structural Verilog
module _3a_rsFlipFlop (
  input  S,
  input  R,
  input  Clock,
  output Q,
  output Q_2
);

  wire nand_1_out, nand_2_out, nand_3_out, nand_4_out, nand_5_out, nand_6_out, not_1_out;

  nand nand_1 (nand_1_out, S, Clock);
  nand nand_2 (nand_2_out, Clock, R);
  nand nand_3 (nand_3_out, nand_1_out, nand_4_out);
  nand nand_4 (nand_4_out, nand_3_out, nand_2_out);
  not not_1 (not_1_out, Clock);
  nand nand_5 (nand_5_out, nand_3_out, not_1_out);
  nand nand_6 (nand_6_out, not_1_out, nand_4_out);
  nand nand_7 (Q, nand_5_out, Q_2);
  nand nand_8 (Q_2, Q, nand_6_out);

  // Notes on the sheet:
  //   Clock: Hz: 10
  //   Maestro
  //   Master-Slave SR Flip-Flop:
  //   Este circuito utiliza dos Latch SR sincrónicos para almacenar un bit de información.
  //   El circuito se divide en dos bloques, un bloque maestro y un bloque esclavo,
  //   los cuales trabajan en conjunto para almacenar el valor de entrada.
  //   Durante el flanco de subida de la señal reloj, la entrada ingresa al RS maestro, 
  //   que está habilitado, mientras que el RS esclavo está deshabilitado.
  //   Durante el flanco de bajada de la señal reloj, la entrada se bloquea y el estado 
  //   del RS maestro se transfiere al RS esclavo, que ahora se encuentra habilitado, 
  //   mientras que el RS maestro está deshabilitado. En este momento, la salida del 
  //   RS esclavo representa el estado actualizado del Flip Flop RS maestro-esclavo.
  //   Cuando S y R se encuentran en 1, el sistema entra en oscilación.
  //   Esclavo
endmodule
