// Digital circuit 3b_jkFlipFlop.dig as structural Verilog
module _3b_jkFlipFlop (
  input  J,
  input  K,
  input  Clock,
  output out_4,
  output out_5
);

  wire nand_1_out, nand_2_out, nand_3_out, nand_4_out, nand_5_out, nand_6_out, nand_7_out, nand_8_out,
       not_1_out, not_2_out, not_3_out;

  nand nand_1 (nand_1_out, out_5, J);
  nand nand_2 (nand_2_out, Clock, K);
  not not_1 (not_1_out, nand_1_out);
  not not_2 (not_2_out, nand_2_out);
  nand nand_3 (nand_3_out, not_1_out, Clock);
  nand nand_4 (nand_4_out, not_2_out, out_4);
  nand nand_5 (nand_5_out, nand_3_out, nand_6_out);
  nand nand_6 (nand_6_out, nand_5_out, nand_4_out);
  not not_3 (not_3_out, Clock);
  nand nand_7 (nand_7_out, nand_5_out, not_3_out);
  nand nand_8 (nand_8_out, not_3_out, nand_6_out);
  nand nand_9 (out_4, nand_7_out, out_5);
  nand nand_10 (out_5, out_4, nand_8_out);

  // Notes on the sheet:
  //   Clock: Hz: 10
  //   Maestro
  //   Master-Slave JK Flip-Flop:
  //   Este circuito utiliza dos Latch JK sincrónicos para almacenar un bit de información.
  //   El circuito se divide en dos bloques, un bloque maestro y un bloque esclavo,
  //   los cuales trabajan en conjunto para almacenar el valor de entrada.
  //   Con el primer flanco de subida de la señal reloj, el flip-flop maestro se activa, permitiendo que los datos de entrada
  //   se carguen. La entrada JK determina el estado de salida del flip-flop maestro en función de su estado 
  //   anterior y de la entrada actual.
  //   Con el primer flanco de bajada de la señal reloj, el flip-flop maestro se desactiva y se bloquea el estado actual 
  //   del flip-flop maestro, asegurándose de que los datos no cambien mientras el flip-flop esclavo procesa la información.
  //   Una vez que el flip-flop maestro está bloqueado, el flip-flop esclavo se activa, cargando el estado del flip-flop maestro 
  //   en el flip-flop esclavo. La entrada JK del flip-flop esclavo también determina su estado de salida.
  //   Con el segundo flanco de subida de la señal reloj, el flip-flop esclavo se desactiva y se bloquea el estado actual 
  //   del flip-flop esclavo, asegurando que los datos no cambien mientras el flip-flop maestro se prepara para recibir la siguiente 
  //   entrada.
  //   Cuando J y K se encuentran en 1 las salidas tienen un comportamiento alternante, pero el sistema no oscila.
  //   Esclavo
endmodule
