// Digital circuit 4_modelo4Pin.dig as structural Verilog
module _4_modelo4Pin (
  input  in_1,
  input  in_2,
  input  in_3,
  input  in_4,
  input  Set,
  input  Clock,
  input  Clear,
  input  Set_2,
  input  Clear_2,
  input  in_14,
  input  in_15,
  input  in_16,
  input  in_17,
  input  Set_3,
  input  Clear_3,
  input  in_21,
  input  in_23,
  input  in_24,
  input  in_26,
  output out_8,
  output out_9,
  output out_10,
  output out_11,
  output out_20,
  output out_22,
  output out_25,
  output out_27
);

  wire d_ff_as_4_q, d_ff_as_6_q, d_ff_as_7_q, d_ff_as_8_q, E0, E1, E2, E3, S0, S1, S2, S3;

  PullDown pulldown_1 (.out(E3));
  D_FF_AS d_ff_as_1 (.Set(Set_2), .D(E3), .C(Clock), .Clr(Clear_2), .Q(out_8));  // open: nQ
  PullDown pulldown_2 (.out(E2));
  D_FF_AS d_ff_as_2 (.Set(Set_2), .D(E2), .C(Clock), .Clr(Clear_2), .Q(out_9));  // open: nQ
  PullDown pulldown_3 (.out(E1));
  D_FF_AS d_ff_as_3 (.Set(Set_2), .D(E1), .C(Clock), .Clr(Clear_2), .Q(out_10));  // open: nQ
  PullDown pulldown_4 (.out(E0));
  D_FF_AS d_ff_as_4 (.Set(Set), .D(in_1), .C(Clock), .Clr(Clear), .Q(d_ff_as_4_q));  // open: nQ
  assign out_20 = ~d_ff_as_4_q ? S3 : 1'bz;  // DriverInvSel driverinvsel_1
  D_FF_AS d_ff_as_5 (.Set(Set_2), .D(E0), .C(Clock), .Clr(Clear_2), .Q(out_11));  // open: nQ
  assign E3 = d_ff_as_4_q ? in_21 : 1'bz;  // Driver driver_1
  D_FF_AS d_ff_as_6 (.Set(Set), .D(in_2), .C(Clock), .Clr(Clear), .Q(d_ff_as_6_q));  // open: nQ
  assign out_22 = ~d_ff_as_6_q ? S2 : 1'bz;  // DriverInvSel driverinvsel_2
  assign E2 = d_ff_as_6_q ? in_23 : 1'bz;  // Driver driver_2
  D_FF_AS d_ff_as_7 (.Set(Set), .D(in_3), .C(Clock), .Clr(Clear), .Q(d_ff_as_7_q));  // open: nQ
  assign out_25 = ~d_ff_as_7_q ? S1 : 1'bz;  // DriverInvSel driverinvsel_3
  assign E1 = d_ff_as_7_q ? in_24 : 1'bz;  // Driver driver_3
  D_FF_AS d_ff_as_8 (.Set(Set), .D(in_4), .C(Clock), .Clr(Clear), .Q(d_ff_as_8_q));  // open: nQ
  assign out_27 = ~d_ff_as_8_q ? S0 : 1'bz;  // DriverInvSel driverinvsel_4
  assign E0 = d_ff_as_8_q ? in_26 : 1'bz;  // Driver driver_4
  D_FF_AS d_ff_as_9 (.Set(Set_3), .D(in_14), .C(Clock), .Clr(Clear_3), .Q(S3));  // open: nQ
  D_FF_AS d_ff_as_10 (.Set(Set_3), .D(in_15), .C(Clock), .Clr(Clear_3), .Q(S2));  // open: nQ
  D_FF_AS d_ff_as_11 (.Set(Set_3), .D(in_16), .C(Clock), .Clr(Clear_3), .Q(S1));  // open: nQ
  D_FF_AS d_ff_as_12 (.Set(Set_3), .D(in_17), .C(Clock), .Clr(Clear_3), .Q(S0));  // open: nQ

  // Other names for the same wires on the sheet: CLK = Clock

  // Notes on the sheet:
  //   Clock: Hz: 10
  //   REGISTRO DE ENTRADA
  //   Almacena el estado del pin, si se configura como entrada
  //   REGISTRO DE CONFIGURACIÓN
  //   Controla la dirección del pin. 
  //   0 = salida ; 1 = entrada
  //   REGISTRO DE SALIDA
  //   Controla el estado del pin, si se configura como salida
endmodule
